# Fritzing sketch Sketch (saved by Fritzing 0.9.3b)

parts:
  Part1 = Arduino Nano (Rev3.0)
  J1 = Basic Servo
  U1 = POT [package=3362u]

nets:
  GND: Part1.GND, J1.gnd, U1.A
  N1: Part1.D9, J1.pulse
  5V: Part1.5V, J1.vcc, U1.E
  N2: Part1.A0, U1.S
